// Logisim project Processor.circ as structural Verilog: 12 circuits, main circuit Processor
module Processor (
  input  Reset,
  input  [3:0] Display_Address
);

  wire alu_1_is, alu_1_is_2, branch_unit_1_isbranchtaken, Clock, control_unit_1_isbeq, control_unit_1_isbgt,
       control_unit_1_iscall, control_unit_1_isimmediate, control_unit_1_isld, control_unit_1_isret,
       control_unit_1_isst, control_unit_1_isubranch, control_unit_1_iswb, ex_ma_1_iscall_2, ex_ma_1_isld_2,
       ex_ma_1_isst_2, ex_ma_1_iswb_2, flags_1_flags_e, flags_1_flags_gt, ma_rw_1_iswb_2, of_ex_1_isbeq_2,
       of_ex_1_isbgt_2, of_ex_1_iscall_2, of_ex_1_isld_2, of_ex_1_isret_2, of_ex_1_isst_2,
       of_ex_1_isubranch_2, of_ex_1_iswb_2;
  wire [1:0] ma_rw_1_isld_2;
  wire [3:0] multiplexer_4_out, multiplexer_6_out, multiplexer_7_out, register_file_1_displayd_2,
       register_file_1_displayd_3;
  wire [12:0] control_unit_1_alusignals, of_ex_1_alu_signals_2;
  wire [23:0] register_file_1_displayd;
  wire [31:0] adder_1_out, adder_2_out, alu_1_aluresult, calculate_immediate_1_branch_target,
       calculate_immediate_1_immx, ex_ma_1_alu_result_2, ex_ma_1_instruction_2, ex_ma_1_op2_2, ex_ma_1_pc_2,
       if_of_1_ins_output, if_of_1_pc_output, ma_rw_1_alu_result_2, ma_rw_1_instruction_2,
       ma_rw_1_ld_result_2, ma_rw_1_pc_2, memory_unit_1_ldresult, multiplexer_1_out, multiplexer_2_out,
       multiplexer_3_out, multiplexer_5_out, of_ex_1_a_2, of_ex_1_b_2, of_ex_1_branch_target_2,
       of_ex_1_instruction_2, of_ex_1_op2_2, of_ex_1_pc_2, PC_q, register_file_1_readd1,
       register_file_1_readd2, rom_1_data;

  OF_EX of_ex_1 (
    .in_16(Reset), .pc(if_of_1_pc_output), .branch_target(calculate_immediate_1_branch_target),
    .B(multiplexer_3_out), .A(register_file_1_readd1), .op2(register_file_1_readd2),
    .instruction(if_of_1_ins_output), .isSt(control_unit_1_isst), .isLd(control_unit_1_isld),
    .isBeq(control_unit_1_isbeq), .isBgt(control_unit_1_isbgt), .isRet(control_unit_1_isret),
    .isWb(control_unit_1_iswb), .isUBranch(control_unit_1_isubranch), .isCall(control_unit_1_iscall),
    .ALU_Signals(control_unit_1_alusignals), .pc_2(of_ex_1_pc_2), .branch_target_2(of_ex_1_branch_target_2),
    .B_2(of_ex_1_b_2), .A_2(of_ex_1_a_2), .op2_2(of_ex_1_op2_2), .instruction_2(of_ex_1_instruction_2),
    .isSt_2(of_ex_1_isst_2), .isLd_2(of_ex_1_isld_2), .isBeq_2(of_ex_1_isbeq_2), .isBgt_2(of_ex_1_isbgt_2),
    .isRet_2(of_ex_1_isret_2), .isWb_2(of_ex_1_iswb_2), .isUBranch_2(of_ex_1_isubranch_2),
    .isCall_2(of_ex_1_iscall_2), .ALU_Signals_2(of_ex_1_alu_signals_2));
  Multiplexer #(.width(32), .enable("false")) multiplexer_1 (
    .in0(of_ex_1_branch_target_2), .in1(of_ex_1_a_2), .out(multiplexer_1_out), .sel(of_ex_1_isret_2));
  EX_MA ex_ma_1 (
    .in_9(Reset), .pc(of_ex_1_pc_2), .ALU_Result(alu_1_aluresult), .op2(of_ex_1_op2_2),
    .instruction(of_ex_1_instruction_2), .isSt(of_ex_1_isst_2), .isLd(of_ex_1_isld_2), .isWb(of_ex_1_iswb_2),
    .isCall(of_ex_1_iscall_2), .pc_2(ex_ma_1_pc_2), .ALU_Result_2(ex_ma_1_alu_result_2),
    .op2_2(ex_ma_1_op2_2), .instruction_2(ex_ma_1_instruction_2), .isSt_2(ex_ma_1_isst_2),
    .isLd_2(ex_ma_1_isld_2), .isWb_2(ex_ma_1_iswb_2), .isCall_2(ex_ma_1_iscall_2));
  MA_RW ma_rw_1 (
    .in_8(Reset), .pc(ex_ma_1_pc_2), .ld_Result(memory_unit_1_ldresult), .ALU_Result(ex_ma_1_alu_result_2),
    .instruction(ex_ma_1_instruction_2), .isLd(ex_ma_1_isld_2), .isWb(ex_ma_1_iswb_2),
    .isCall(ex_ma_1_iscall_2), .pc_2(ma_rw_1_pc_2), .ld_Result_2(ma_rw_1_ld_result_2),
    .ALU_Result_2(ma_rw_1_alu_result_2), .instruction_2(ma_rw_1_instruction_2), .isLd_2(ma_rw_1_isld_2[0]),
    .isWb_2(ma_rw_1_iswb_2), .isCall_2(ma_rw_1_isld_2[1]));
  Register #(.width(32), .trigger("falling")) PC (
    .D(multiplexer_5_out), .Q(PC_q), .clk(Clock), .clr(Reset));  // open: en
  Calculate_Immediate calculate_immediate_1 (
    .ins(if_of_1_ins_output), .immx(calculate_immediate_1_immx), .pc(if_of_1_pc_output),
    .branch_target(calculate_immediate_1_branch_target));
  Adder #(.width(32)) adder_1 (.a(ma_rw_1_pc_2), .b(32'h4), .out(adder_1_out));  // open: cin, cout
  ALU alu_1 (
    .A(of_ex_1_a_2), .B(of_ex_1_b_2), .ALUsignals(of_ex_1_alu_signals_2), .aluResult(alu_1_aluresult),
    .is(alu_1_is), .is_2(alu_1_is_2));
  Multiplexer #(.select(2), .width(32), .enable("false")) multiplexer_2 (
    .in0(ma_rw_1_alu_result_2), .in1(ma_rw_1_ld_result_2), .in2(adder_1_out), .out(multiplexer_2_out),
    .sel(ma_rw_1_isld_2));  // open: in3
  Multiplexer #(.width(32), .enable("false")) multiplexer_3 (
    .in0(register_file_1_readd2), .in1(calculate_immediate_1_immx), .out(multiplexer_3_out),
    .sel(control_unit_1_isimmediate));
  IF_OF if_of_1 (
    .PC_Input(PC_q), .Ins_Input(rom_1_data), .PC_Output(if_of_1_pc_output), .Ins_Output(if_of_1_ins_output),
    .in_3(Reset));
  Memory_Unit memory_unit_1 (
    .MAR(ex_ma_1_alu_result_2), .ldResult(memory_unit_1_ldresult), .MDR(ex_ma_1_op2_2),
    .isSt(ex_ma_1_isst_2), .isLd(ex_ma_1_isld_2), .Clock(Clock), .Reset(Reset));
  Clock u_Clock (.out(Clock));
  Adder #(.width(32)) adder_2 (.a(32'h4), .b(PC_q), .out(adder_2_out));  // open: cin, cout
  ROM #(.addrWidth(24), .dataWidth(32)) rom_1 (.addr(PC_q[25:2]), .data(rom_1_data));  // open: sel
  Flags flags_1 (
    .isCmp(of_ex_1_alu_signals_2[0]), .is(alu_1_is), .is_2(alu_1_is_2), .flags_GT(flags_1_flags_gt),
    .flags_E(flags_1_flags_e));
  Multiplexer #(.width(4), .enable("false")) multiplexer_4 (
    .in0(ma_rw_1_instruction_2[25:22]), .in1(4'b1111), .out(multiplexer_4_out), .sel(ma_rw_1_isld_2[1]));
  Hex_Digit_Display hex_digit_display_1 (.value(register_file_1_displayd_3));  // open: dp
  Multiplexer #(.width(32), .enable("false")) multiplexer_5 (
    .in0(adder_2_out), .in1(multiplexer_1_out), .out(multiplexer_5_out), .sel(branch_unit_1_isbranchtaken));
  Multiplexer #(.width(4), .enable("false")) multiplexer_6 (
    .in0(if_of_1_ins_output[17:14]), .in1(if_of_1_ins_output[25:22]), .out(multiplexer_6_out),
    .sel(control_unit_1_isst));
  Branch_Unit branch_unit_1 (
    .isBeq(of_ex_1_isbeq_2), .isUBranch(of_ex_1_isubranch_2), .flags_E(flags_1_flags_e),
    .isBgt(of_ex_1_isbgt_2), .flags_GT(flags_1_flags_gt), .isBranchTaken(branch_unit_1_isbranchtaken));
  Hex_Digit_Display hex_digit_display_2 (.value(register_file_1_displayd_2));  // open: dp
  Multiplexer #(.width(4), .enable("false")) multiplexer_7 (
    .in0(if_of_1_ins_output[21:18]), .in1(4'b1111), .out(multiplexer_7_out), .sel(control_unit_1_isret));
  Hex_Digit_Display hex_digit_display_3 (.value(register_file_1_displayd[23:20]));  // open: dp
  Register_File register_file_1 (
    .ReadA1(multiplexer_7_out), .ReadA2(multiplexer_6_out), .WriteE(ma_rw_1_iswb_2),
    .WriteD(multiplexer_2_out), .ReadD1(register_file_1_readd1), .ReadD2(register_file_1_readd2),
    .Clock(Clock), .Reset(Reset),
    .DisplayD({register_file_1_displayd_3, register_file_1_displayd_2, register_file_1_displayd}),
    .DisplayA(Display_Address), .WriteA(multiplexer_4_out));
  Hex_Digit_Display hex_digit_display_4 (.value(register_file_1_displayd[15:12]));  // open: dp
  Hex_Digit_Display hex_digit_display_5 (.value(register_file_1_displayd[19:16]));  // open: dp
  Control_Unit control_unit_1 (
    .isSt(control_unit_1_isst), .isLd(control_unit_1_isld), .isBeq(control_unit_1_isbeq),
    .isBgt(control_unit_1_isbgt), .isRet(control_unit_1_isret), .I_bit(if_of_1_ins_output[26]),
    .isImmediate(control_unit_1_isimmediate), .opcode(if_of_1_ins_output[31:27]), .isWb(control_unit_1_iswb),
    .isUbranch(control_unit_1_isubranch), .isCall(control_unit_1_iscall),
    .ALUsignals(control_unit_1_alusignals));
  Hex_Digit_Display hex_digit_display_6 (.value(register_file_1_displayd[11:8]));  // open: dp
  Hex_Digit_Display hex_digit_display_7 (.value(register_file_1_displayd[7:4]));  // open: dp
  Hex_Digit_Display hex_digit_display_8 (.value(register_file_1_displayd[3:0]));  // open: dp

  // Notes on the sheet:
  //   ALU
  //   Memory
  //   Unit
  //   isBranchTaken
  //   Flags
  //   isCmp
  //   SINGLE CYCLE PROCESSOR
  //   isBranchTaken
  //   Instruction Memory
  //   contents of rom_1 (hex, n*v repeats v):
  //   4c00000a 98000002 90000000 2c000001 88000003 4c400001 a0000000 fb80008 7c380000 7ff80004 c000001
  //   9ffffff8 77f80004 74380000 7b80008 10404000 a0000000
  //   GT
  //   E
  //   rs2
  //   Branch
  //   Unit
  //   rs1
  //   rd
  //   isSt
  //   Register
  //   File
  //   op1
  //   op2
  //   isRet
  //   E
  //   A
  //   D
  //   Display Register
  //   Control
  //   Unit
endmodule

module Control_Unit (
  input  I_bit,
  input  [4:0] opcode,
  output isSt,
  output isLd,
  output isBeq,
  output isBgt,
  output isRet,
  output isImmediate,
  output isWb,
  output isUbranch,
  output isCall,
  output [12:0] ALUsignals
);

  wire and_6_out, and_7_out, and_8_out, and_9_out, and_10_out, and_12_out, and_13_out, nand_1_out;

  nand nand_1 (nand_1_out, opcode[0], opcode[1]);
  and and_1 (isSt, opcode[0], opcode[1], opcode[2], opcode[3], ~opcode[4]);  // AND_Gate
  and and_2 (isLd, ~opcode[0], opcode[1], opcode[2], opcode[3], ~opcode[4]);  // AND_Gate
  and and_3 (isBeq, ~opcode[0], ~opcode[1], ~opcode[2], ~opcode[3], opcode[4]);  // AND_Gate
  and and_4 (isBgt, opcode[0], ~opcode[1], ~opcode[2], ~opcode[3], opcode[4]);  // AND_Gate
  and and_5 (isRet, ~opcode[0], ~opcode[1], opcode[2], ~opcode[3], opcode[4]);  // AND_Gate
  and and_6 (and_6_out, opcode[0], ~opcode[1], opcode[2], ~opcode[4]);  // AND_Gate
  and and_7 (and_7_out, opcode[0], opcode[2], opcode[3], ~opcode[4]);  // AND_Gate
  and and_8 (and_8_out, opcode[4], nand_1_out);
  and and_9 (and_9_out, opcode[1], ~opcode[2], ~opcode[3], opcode[4]);  // AND_Gate
  and and_10 (and_10_out, ~opcode[0], ~opcode[1], opcode[2], ~opcode[3], opcode[4]);  // AND_Gate
  and and_11 (isCall, opcode[0], opcode[1], ~opcode[2], ~opcode[3], opcode[4]);  // AND_Gate
  and and_12 (and_12_out, ~opcode[0], ~opcode[1], ~opcode[2], ~opcode[3], ~opcode[4]);  // AND_Gate
  and and_13 (and_13_out, opcode[1], opcode[2], opcode[3], ~opcode[4]);  // AND_Gate
  and isSub (ALUsignals[2], opcode[0], ~opcode[1], ~opcode[2], ~opcode[3], ~opcode[4]);  // AND_Gate
  and isCmp (ALUsignals[0], opcode[0], ~opcode[1], opcode[2], ~opcode[3], ~opcode[4]);  // AND_Gate
  and isMul (ALUsignals[3], ~opcode[0], opcode[1], ~opcode[2], ~opcode[3], ~opcode[4]);  // AND_Gate
  and isDiv (ALUsignals[4], opcode[0], opcode[1], ~opcode[2], ~opcode[3], ~opcode[4]);  // AND_Gate
  and isMod (ALUsignals[5], ~opcode[0], ~opcode[1], opcode[2], ~opcode[3], ~opcode[4]);  // AND_Gate
  and isLsl (ALUsignals[7], ~opcode[0], opcode[1], ~opcode[2], opcode[3], ~opcode[4]);  // AND_Gate
  and isLsr (ALUsignals[8], opcode[0], opcode[1], ~opcode[2], opcode[3], ~opcode[4]);  // AND_Gate
  and isAsr (ALUsignals[9], ~opcode[0], ~opcode[1], opcode[2], opcode[3], ~opcode[4]);  // AND_Gate
  and isOr (ALUsignals[12], opcode[0], opcode[1], opcode[2], ~opcode[3], ~opcode[4]);  // AND_Gate
  and isAnd (ALUsignals[11], ~opcode[0], opcode[1], opcode[2], ~opcode[3], ~opcode[4]);  // AND_Gate
  and isNot (ALUsignals[10], ~opcode[0], ~opcode[1], ~opcode[2], opcode[3], ~opcode[4]);  // AND_Gate
  and isMov (ALUsignals[6], opcode[0], ~opcode[1], ~opcode[2], opcode[3], ~opcode[4]);  // AND_Gate
  or or_1 (isUbranch, and_9_out, and_10_out);
  or isAdd (ALUsignals[1], and_12_out, and_13_out);
  nor nor_1 (isWb, and_6_out, and_7_out, and_8_out);

  assign isImmediate = I_bit;

  // Notes on the sheet:
  //   op1
  //   op2
  //   op3
  //   op4
  //   op5
endmodule

module Register_File (
  input  Clock,
  input  Reset,
  input  [31:0] WriteD,
  input  [3:0] ReadA1,
  input  WriteE,
  input  [3:0] WriteA,
  input  [3:0] ReadA2,
  input  [3:0] DisplayA,
  output [31:0] ReadD1,
  output [31:0] ReadD2,
  output [31:0] DisplayD
);

  wire demultiplexer_1_out0, demultiplexer_1_out1, demultiplexer_1_out2, demultiplexer_1_out3,
       demultiplexer_1_out4, demultiplexer_1_out5, demultiplexer_1_out6, demultiplexer_1_out7,
       demultiplexer_1_out8, demultiplexer_1_out9, demultiplexer_1_out10, demultiplexer_1_out11,
       demultiplexer_1_out12, demultiplexer_1_out13, demultiplexer_1_out14, demultiplexer_1_out15,
       multiplexer_2_out, or_1_out, or_2_out;
  wire [31:0] multiplexer_1_out, r0_q, r1_q, r2_q, r3_q, r4_q, r5_q, r6_q, r7_q, r8_q, r9_q, r10_q, r11_q,
       r12_q, r13_q, r14_q, r15_q;

  Demultiplexer #(.select(4), .disabled(0), .enable("false")) demultiplexer_1 (
    .out0(demultiplexer_1_out0), .out1(demultiplexer_1_out1), .out2(demultiplexer_1_out2),
    .out3(demultiplexer_1_out3), .out4(demultiplexer_1_out4), .out5(demultiplexer_1_out5),
    .out6(demultiplexer_1_out6), .out7(demultiplexer_1_out7), .out8(demultiplexer_1_out8),
    .out9(demultiplexer_1_out9), .out10(demultiplexer_1_out10), .out11(demultiplexer_1_out11),
    .out12(demultiplexer_1_out12), .out13(demultiplexer_1_out13), .out14(demultiplexer_1_out14),
    .out15(demultiplexer_1_out15), .in(WriteE), .sel(WriteA));
  Multiplexer #(.width(32), .enable("false")) multiplexer_1 (
    .in0(WriteD), .in1(32'h3fffffc), .out(multiplexer_1_out), .sel(Reset));
  or or_1 (or_1_out, demultiplexer_1_out14, Reset);
  or or_2 (or_2_out, Clock, Reset);
  Multiplexer #(.enable("false")) multiplexer_2 (.in0(or_2_out), .out(multiplexer_2_out), .sel(1'b0));  // open: in1
  Register #(.width(32)) r0 (.D(WriteD), .en(demultiplexer_1_out0), .Q(r0_q), .clk(Clock), .clr(Reset));
  Register #(.width(32)) r1 (.D(WriteD), .en(demultiplexer_1_out1), .Q(r1_q), .clk(Clock), .clr(Reset));
  Register #(.width(32)) r2 (.D(WriteD), .en(demultiplexer_1_out2), .Q(r2_q), .clk(Clock), .clr(Reset));
  Register #(.width(32)) r3 (.D(WriteD), .en(demultiplexer_1_out3), .Q(r3_q), .clk(Clock), .clr(Reset));
  Register #(.width(32)) r4 (.D(WriteD), .en(demultiplexer_1_out4), .Q(r4_q), .clk(Clock), .clr(Reset));
  Register #(.width(32)) r5 (.D(WriteD), .en(demultiplexer_1_out5), .Q(r5_q), .clk(Clock), .clr(Reset));
  Register #(.width(32)) r6 (.D(WriteD), .en(demultiplexer_1_out6), .Q(r6_q), .clk(Clock), .clr(Reset));
  Register #(.width(32)) r7 (.D(WriteD), .en(demultiplexer_1_out7), .Q(r7_q), .clk(Clock), .clr(Reset));
  Register #(.width(32)) r8 (.D(WriteD), .en(demultiplexer_1_out8), .Q(r8_q), .clk(Clock), .clr(Reset));
  Register #(.width(32)) r9 (.D(WriteD), .en(demultiplexer_1_out9), .Q(r9_q), .clk(Clock), .clr(Reset));
  Register #(.width(32)) r10 (.D(WriteD), .en(demultiplexer_1_out10), .Q(r10_q), .clk(Clock), .clr(Reset));
  Register #(.width(32)) r11 (.D(WriteD), .en(demultiplexer_1_out11), .Q(r11_q), .clk(Clock), .clr(Reset));
  Register #(.width(32)) r12 (.D(WriteD), .en(demultiplexer_1_out12), .Q(r12_q), .clk(Clock), .clr(Reset));
  Register #(.width(32)) r13 (.D(WriteD), .en(demultiplexer_1_out13), .Q(r13_q), .clk(Clock), .clr(Reset));
  Register #(.width(32)) r14 (.D(multiplexer_1_out), .en(or_1_out), .Q(r14_q), .clk(multiplexer_2_out));  // open: clr
  Register #(.width(32)) r15 (.D(WriteD), .en(demultiplexer_1_out15), .Q(r15_q), .clk(Clock), .clr(Reset));
  Multiplexer #(.select(4), .width(32), .disabled(0), .enable("false")) multiplexer_3 (
    .in0(r0_q), .in1(r1_q), .in2(r2_q), .in3(r3_q), .in4(r4_q), .in5(r5_q), .in6(r6_q), .in7(r7_q),
    .in8(r8_q), .in9(r9_q), .in10(r10_q), .in11(r11_q), .in12(r12_q), .in13(r13_q), .in14(r14_q),
    .in15(r15_q), .out(ReadD1), .sel(ReadA1));
  Multiplexer #(.select(4), .width(32), .disabled(0), .enable("false")) multiplexer_4 (
    .in0(r0_q), .in1(r1_q), .in2(r2_q), .in3(r3_q), .in4(r4_q), .in5(r5_q), .in6(r6_q), .in7(r7_q),
    .in8(r8_q), .in9(r9_q), .in10(r10_q), .in11(r11_q), .in12(r12_q), .in13(r13_q), .in14(r14_q),
    .in15(r15_q), .out(ReadD2), .sel(ReadA2));
  Multiplexer #(.select(4), .width(32), .disabled(0), .enable("false")) multiplexer_5 (
    .in0(r0_q), .in1(r1_q), .in2(r2_q), .in3(r3_q), .in4(r4_q), .in5(r5_q), .in6(r6_q), .in7(r7_q),
    .in8(r8_q), .in9(r9_q), .in10(r10_q), .in11(r11_q), .in12(r12_q), .in13(r13_q), .in14(r14_q),
    .in15(r15_q), .out(DisplayD), .sel(DisplayA));
endmodule

module ALU (
  input  [31:0] A,
  input  [31:0] B,
  input  [12:0] ALUsignals,
  output [31:0] aluResult,
  output is,
  output is_2
);

  wire [31:0] adder_1_out, and_1_out, divider_1_out, divider_1_rem, multiplier_1_out, not_1_out, or_1_out,
       shifter_1_out, shifter_2_out, shifter_3_out, subtractor_1_out;

  Adder #(.width(32)) adder_1 (.a(A), .b(B), .out(adder_1_out));  // open: cin, cout
  Subtractor #(.width(32)) subtractor_1 (.a(A), .b(B), .out(subtractor_1_out));  // open: bin, bout
  Multiplier #(.width(32)) multiplier_1 (.a(A), .b(B), .out(multiplier_1_out));  // open: cin, cout
  Divider #(.width(32)) divider_1 (.a(A), .b(B), .out(divider_1_out), .rem(divider_1_rem));  // open: upper
  Comparator #(.width(32)) comparator_1 (.a(A), .b(B), .gt(is), .eq(is_2));  // open: lt
  Shifter #(.width(32)) shifter_1 (.in(A), .\dist (B[4:0]), .out(shifter_1_out));
  Shifter #(.width(32), .shift("lr")) shifter_2 (.in(A), .\dist (B[4:0]), .out(shifter_2_out));
  Shifter #(.width(32), .shift("ar")) shifter_3 (.in(A), .\dist (B[4:0]), .out(shifter_3_out));
  assign not_1_out = ~B;  // NOT_Gate not_1, 32 bits wide
  assign and_1_out = A & B;  // AND_Gate and_1, 32 bits wide
  assign or_1_out = A | B;  // OR_Gate or_1, 32 bits wide
  assign aluResult = ALUsignals[1] ? adder_1_out : 32'bz;  // Controlled_Buffer controlled_buffer_1
  assign aluResult = ALUsignals[2] ? subtractor_1_out : 32'bz;  // Controlled_Buffer controlled_buffer_2
  assign aluResult = ALUsignals[3] ? multiplier_1_out : 32'bz;  // Controlled_Buffer controlled_buffer_3
  assign aluResult = ALUsignals[4] ? divider_1_out : 32'bz;  // Controlled_Buffer controlled_buffer_4
  assign aluResult = ALUsignals[5] ? divider_1_rem : 32'bz;  // Controlled_Buffer controlled_buffer_5
  assign aluResult = ALUsignals[6] ? B : 32'bz;  // Controlled_Buffer controlled_buffer_6
  assign aluResult = ALUsignals[7] ? shifter_1_out : 32'bz;  // Controlled_Buffer controlled_buffer_7
  assign aluResult = ALUsignals[8] ? shifter_2_out : 32'bz;  // Controlled_Buffer controlled_buffer_8
  assign aluResult = ALUsignals[9] ? shifter_3_out : 32'bz;  // Controlled_Buffer controlled_buffer_9
  assign aluResult = ALUsignals[10] ? not_1_out : 32'bz;  // Controlled_Buffer controlled_buffer_10
  assign aluResult = ALUsignals[11] ? and_1_out : 32'bz;  // Controlled_Buffer controlled_buffer_11
  assign aluResult = ALUsignals[12] ? or_1_out : 32'bz;  // Controlled_Buffer controlled_buffer_12

  // Notes on the sheet:
  //   add
  //   sub
  //   mul
  //   div
  //   cmp
  //   lsr
  //   mod
  //   lsl
  //   asr
endmodule

module Flags (
  input  isCmp,
  input  is,
  input  is_2,
  output flags_GT,
  output flags_E
);

  D_Flip_Flop #(.trigger("high")) d_ff_1 (.clk(isCmp), .D(is), .Q(flags_GT));  // open: Qn, preset, en, reset
  D_Flip_Flop #(.trigger("high")) d_ff_2 (.clk(isCmp), .D(is_2), .Q(flags_E));  // open: Qn, preset, en, reset
endmodule

module Branch_Unit (
  input  isUBranch,
  input  isBeq,
  input  flags_E,
  input  isBgt,
  input  flags_GT,
  output isBranchTaken
);

  wire and_1_out, and_2_out;

  and and_1 (and_1_out, isBeq, flags_E);
  and and_2 (and_2_out, isBgt, flags_GT);
  or or_1 (isBranchTaken, isUBranch, and_1_out, and_2_out);
endmodule

module Memory_Unit (
  input  [31:0] MAR,
  input  isLd,
  input  [31:0] MDR,
  input  isSt,
  input  Clock,
  input  Reset,
  output [31:0] ldResult
);

  RAM #(.addrWidth(24), .dataWidth(32), .bus("separate")) ram_1 (
    .addr(MAR[25:2]), .din(MDR), .data(ldResult), .str(isSt), .clk(Clock), .ld(isLd), .clr(Reset));  // open: sel
endmodule

module Calculate_Immediate (
  input  [31:0] ins,
  input  [31:0] pc,
  output [31:0] immx,
  output [31:0] branch_target
);

  wire [31:0] bit_extender_1_out, bit_extender_2_out, bit_extender_3_out, shifter_1_out, shifter_2_out;

  assign bit_extender_1_out = {{5{ins[26]}}, ins[26:0]};  // Bit_Extender bit_extender_1
  assign bit_extender_2_out = {{16{1'b0}}, ins[15:0]};  // Bit_Extender bit_extender_2
  Shifter #(.width(32)) shifter_1 (.in(bit_extender_1_out), .\dist (5'b00010), .out(shifter_1_out));
  assign bit_extender_3_out = {{16{ins[15]}}, ins[15:0]};  // Bit_Extender bit_extender_3
  Shifter #(.width(32)) shifter_2 (.in(bit_extender_2_out), .\dist (5'b10000), .out(shifter_2_out));
  Adder #(.width(32)) adder_1 (.a(shifter_1_out), .b(pc), .out(branch_target));  // open: cin, cout
  Multiplexer #(.select(2), .width(32), .enable("false")) multiplexer_1 (
    .in0(bit_extender_3_out), .in1(bit_extender_2_out), .in2(shifter_2_out), .out(immx), .sel(ins[17:16]));  // open: in3

  // Notes on the sheet:
  //   modifier bits
  //   default
  //   unsigned
  //   high
endmodule

module IF_OF (
  input  [31:0] PC_Input,
  input  [31:0] Ins_Input,
  input  in_3,
  output [31:0] PC_Output,
  output [31:0] Ins_Output
);

  wire clock_1_out;

  Clock clock_1 (.out(clock_1_out));
  Register #(.width(32)) PC (.D(PC_Input), .Q(PC_Output), .clk(clock_1_out), .clr(in_3));  // open: en
  Register #(.width(32)) Instruction (.D(Ins_Input), .Q(Ins_Output), .clk(clock_1_out), .clr(in_3));  // open: en
endmodule

module OF_EX (
  input  [31:0] pc,
  input  [31:0] branch_target,
  input  [31:0] B,
  input  [31:0] A,
  input  [31:0] op2,
  input  [31:0] instruction,
  input  isSt,
  input  isLd,
  input  isBeq,
  input  isBgt,
  input  isRet,
  input  isWb,
  input  isUBranch,
  input  isCall,
  input  [12:0] ALU_Signals,
  input  in_16,
  output [31:0] pc_2,
  output [31:0] branch_target_2,
  output [31:0] B_2,
  output [31:0] A_2,
  output [31:0] op2_2,
  output [31:0] instruction_2,
  output isSt_2,
  output isLd_2,
  output isBeq_2,
  output isBgt_2,
  output isRet_2,
  output isWb_2,
  output isUBranch_2,
  output isCall_2,
  output [12:0] ALU_Signals_2
);

  wire clock_1_out;

  Clock clock_1 (.out(clock_1_out));
  Register #(.width(32)) register_1 (.D(pc), .Q(pc_2), .clk(clock_1_out), .clr(in_16));  // open: en
  Register #(.width(32)) register_2 (
    .D(branch_target), .Q(branch_target_2), .clk(clock_1_out), .clr(in_16));  // open: en
  Register #(.width(32)) register_3 (.D(B), .Q(B_2), .clk(clock_1_out), .clr(in_16));  // open: en
  Register #(.width(32)) register_4 (.D(A), .Q(A_2), .clk(clock_1_out), .clr(in_16));  // open: en
  Register #(.width(32)) register_5 (.D(op2), .Q(op2_2), .clk(clock_1_out), .clr(in_16));  // open: en
  Register #(.width(32)) register_6 (.D(instruction), .Q(instruction_2), .clk(clock_1_out), .clr(in_16));  // open: en
  Register #(.width(1)) register_7 (.D(isSt), .Q(isSt_2), .clk(clock_1_out), .clr(in_16));  // open: en
  Register #(.width(1)) register_8 (.D(isLd), .Q(isLd_2), .clk(clock_1_out), .clr(in_16));  // open: en
  Register #(.width(1)) register_9 (.D(isBgt), .Q(isBgt_2), .clk(clock_1_out), .clr(in_16));  // open: en
  Register #(.width(1)) register_10 (.D(isBeq), .Q(isBeq_2), .clk(clock_1_out), .clr(in_16));  // open: en
  Register #(.width(1)) register_11 (.D(isRet), .Q(isRet_2), .clk(clock_1_out), .clr(in_16));  // open: en
  Register #(.width(1)) register_12 (.D(isWb), .Q(isWb_2), .clk(clock_1_out), .clr(in_16));  // open: en
  Register #(.width(1)) register_13 (.D(isCall), .Q(isCall_2), .clk(clock_1_out), .clr(in_16));  // open: en
  Register #(.width(1)) register_14 (.D(isUBranch), .Q(isUBranch_2), .clk(clock_1_out), .clr(in_16));  // open: en
  Register #(.width(13)) register_15 (.D(ALU_Signals), .Q(ALU_Signals_2), .clk(clock_1_out), .clr(in_16));  // open: en
endmodule

module EX_MA (
  input  [31:0] pc,
  input  [31:0] ALU_Result,
  input  [31:0] op2,
  input  [31:0] instruction,
  input  isSt,
  input  isLd,
  input  isWb,
  input  isCall,
  input  in_9,
  output [31:0] pc_2,
  output [31:0] ALU_Result_2,
  output [31:0] op2_2,
  output [31:0] instruction_2,
  output isSt_2,
  output isLd_2,
  output isWb_2,
  output isCall_2
);

  wire clock_1_out;

  Clock clock_1 (.out(clock_1_out));
  Register #(.width(32)) register_1 (.D(pc), .Q(pc_2), .clk(clock_1_out), .clr(in_9));  // open: en
  Register #(.width(32)) register_2 (.D(ALU_Result), .Q(ALU_Result_2), .clk(clock_1_out), .clr(in_9));  // open: en
  Register #(.width(32)) register_3 (.D(op2), .Q(op2_2), .clk(clock_1_out), .clr(in_9));  // open: en
  Register #(.width(32)) register_4 (.D(instruction), .Q(instruction_2), .clk(clock_1_out), .clr(in_9));  // open: en
  Register #(.width(1)) register_5 (.D(isSt), .Q(isSt_2), .clk(clock_1_out), .clr(in_9));  // open: en
  Register #(.width(1)) register_6 (.D(isLd), .Q(isLd_2), .clk(clock_1_out), .clr(in_9));  // open: en
  Register #(.width(1)) register_7 (.D(isWb), .Q(isWb_2), .clk(clock_1_out), .clr(in_9));  // open: en
  Register #(.width(1)) register_8 (.D(isCall), .Q(isCall_2), .clk(clock_1_out), .clr(in_9));  // open: en
endmodule

module MA_RW (
  input  [31:0] pc,
  input  [31:0] ld_Result,
  input  [31:0] ALU_Result,
  input  [31:0] instruction,
  input  isLd,
  input  isWb,
  input  isCall,
  input  in_8,
  output [31:0] pc_2,
  output [31:0] ld_Result_2,
  output [31:0] ALU_Result_2,
  output [31:0] instruction_2,
  output isLd_2,
  output isWb_2,
  output isCall_2
);

  wire clock_1_out;

  Clock clock_1 (.out(clock_1_out));
  Register #(.width(32)) register_1 (.D(pc), .Q(pc_2), .clk(clock_1_out), .clr(in_8));  // open: en
  Register #(.width(32)) register_2 (.D(ld_Result), .Q(ld_Result_2), .clk(clock_1_out), .clr(in_8));  // open: en
  Register #(.width(32)) register_3 (.D(ALU_Result), .Q(ALU_Result_2), .clk(clock_1_out), .clr(in_8));  // open: en
  Register #(.width(32)) register_4 (.D(instruction), .Q(instruction_2), .clk(clock_1_out), .clr(in_8));  // open: en
  Register #(.width(1)) register_5 (.D(isLd), .Q(isLd_2), .clk(clock_1_out), .clr(in_8));  // open: en
  Register #(.width(1)) register_6 (.D(isWb), .Q(isWb_2), .clk(clock_1_out), .clr(in_8));  // open: en
  Register #(.width(1)) register_7 (.D(isCall), .Q(isCall_2), .clk(clock_1_out), .clr(in_8));  // open: en
endmodule
